// Logisim project Exp2_ALU.circ as structural Verilog: 4 circuits, main circuit 1-bit ALU
module _1_bit_ALU (
  input  A,
  input  B,
  input  [1:0] in_3,
  input  Cin,
  output out_5,
  output out_6
);

  wire adder_1_out, and_1_out, or_1_out, xor_1_out;

  or or_1 (or_1_out, A, B);
  Adder #(.width(1)) adder_1 (.a(A), .b(B), .out(adder_1_out), .cin(Cin), .cout(out_6));
  and and_1 (and_1_out, A, B);
  xor xor_1 (xor_1_out, A, B);
  Multiplexer #(.select(2)) multiplexer_1 (
    .in0(and_1_out), .in1(or_1_out), .in2(xor_1_out), .in3(adder_1_out), .out(out_5), .sel(in_3));  // open: en

  // Notes on the sheet:
  //   Experiment 2: ALU
endmodule

module _4_bit_ALU (
  input  in_1,
  input  [3:0] in_2,
  input  [3:0] B,
  output [3:0] out_4,
  output out_5
);

  wire n1_bit_alu_1_out_6, n1_bit_alu_2_out_6, n1_bit_alu_3_out_6;

  _1_bit_ALU u_1_bit_alu_1 (
    .A(in_2[0]), .B(B[0]), .Cin(in_1), .out_5(out_4[0]), .out_6(n1_bit_alu_1_out_6));  // open: in_3
  _1_bit_ALU u_1_bit_alu_2 (
    .A(in_2[1]), .B(B[1]), .Cin(n1_bit_alu_1_out_6), .out_5(out_4[1]), .out_6(n1_bit_alu_2_out_6));  // open: in_3
  _1_bit_ALU u_1_bit_alu_3 (
    .A(in_2[2]), .B(B[2]), .Cin(n1_bit_alu_2_out_6), .out_5(out_4[2]), .out_6(n1_bit_alu_3_out_6));  // open: in_3
  _1_bit_ALU u_1_bit_alu_4 (
    .A(in_2[3]), .B(B[3]), .Cin(n1_bit_alu_3_out_6), .out_5(out_4[3]), .out_6(out_5));  // open: in_3

  // Notes on the sheet:
  //   A
  //   4-BIT ALU
endmodule

module test_1 (
  input  in_1,
  input  in_2,
  input  [1:0] in_3,
  input  in_4,
  output out_5,
  output out_6
);

  wire adder_1_out, and_1_out, or_1_out, xor_1_out;

  and and_1 (and_1_out, in_1, in_2);
  or or_1 (or_1_out, in_1, in_2);
  xor xor_1 (xor_1_out, in_1, in_2);
  Adder #(.width(1)) adder_1 (.a(in_1), .b(in_2), .out(adder_1_out), .cin(in_4), .cout(out_6));
  Multiplexer #(.select(2)) multiplexer_1 (
    .in0(and_1_out), .in1(or_1_out), .in2(xor_1_out), .in3(adder_1_out), .out(out_5), .sel(in_3));  // open: en
endmodule

module _4_bit_test (
  input  [3:0] in_1,
  input  [3:0] in_2,
  output [3:0] out_3,
  output out_4
);

  wire test_1_1_out_6, test_1_2_out_6, test_1_3_out_6;

  test_1 test_1_1 (.out_5(out_3[0]), .out_6(test_1_1_out_6), .in_1(in_1[0]), .in_2(in_2[0]));  // open: in_3, in_4
  test_1 test_1_2 (
    .out_5(out_3[1]), .out_6(test_1_2_out_6), .in_4(test_1_1_out_6), .in_1(in_1[1]), .in_2(in_2[1]));  // open: in_3
  test_1 test_1_3 (
    .out_5(out_3[2]), .out_6(test_1_3_out_6), .in_4(test_1_2_out_6), .in_1(in_1[2]), .in_2(in_2[2]));  // open: in_3
  test_1 test_1_4 (
    .out_5(out_3[3]), .out_6(out_4), .in_4(test_1_3_out_6), .in_1(in_1[3]), .in_2(in_2[3]));  // open: in_3
endmodule
