// Logisim project as1.circ as structural Verilog: 5 circuits, main circuit 1bit-ALU
// ALU
module _1bit_ALU (
  input  A,
  input  [1:0] S,
  input  Cin,
  input  B,
  output \output ,
  output Cout
);

  wire adder_1_out, and_1_out, or_1_out, xor_1_out;

  and and_1 (and_1_out, A, B);
  or or_1 (or_1_out, A, B);
  xor xor_1 (xor_1_out, A, B);
  Adder #(.width(1)) adder_1 (.a(A), .b(B), .out(adder_1_out), .cin(Cin), .cout(Cout));
  Multiplexer #(.select(2), .enable("false")) multiplexer_1 (
    .in0(and_1_out), .in1(or_1_out), .in2(xor_1_out), .in3(adder_1_out), .out(\output ), .sel(S));

  // Notes on the sheet:
  //   1-bit-ALU using and, or,xor and adder
endmodule

module _4bit_ALU (
  input  [1:0] in_1,
  input  [3:0] A,
  input  in_3,
  input  [3:0] B,
  output [3:0] out_5,
  output out_6
);

  wire _1_bit_ALU_2_cout, _1_bit_ALU_3_cout, _1_bit_ALU_cout;

  _1bit_ALU _1_bit_ALU (.A(A[0]), .S(in_1), .Cin(in_3), .B(B[0]), .\output (out_5[0]), .Cout(_1_bit_ALU_cout));
  _1bit_ALU _1_bit_ALU_2 (
    .A(A[1]), .S(in_1), .Cin(_1_bit_ALU_cout), .B(B[1]), .\output (out_5[1]), .Cout(_1_bit_ALU_2_cout));
  _1bit_ALU _1_bit_ALU_3 (
    .A(A[2]), .S(in_1), .Cin(_1_bit_ALU_2_cout), .B(B[2]), .\output (out_5[2]), .Cout(_1_bit_ALU_3_cout));
  _1bit_ALU _1_bit_ALU_4 (.A(A[3]), .S(in_1), .Cin(_1_bit_ALU_3_cout), .B(B[3]), .\output (out_5[3]), .Cout(out_6));

  // Notes on the sheet:
  //   4-bit-ALU using 1 bit-ALU.
endmodule

module ALU_consist_All_Logic_Gate (
  input  A,
  input  [3:0] S,
  input  Cin,
  input  B,
  output Output,
  output Cout
);

  wire adder_1_cout, adder_1_out, and_1_out, divider_1_out, multiplier_1_cout, multiplier_1_out, nand_1_out,
       nor_1_out, not_1_out, or_1_out, subtractor_1_bout, subtractor_1_out, xnor_1_out, xor_1_out, xor_2_out;

  Adder #(.width(1)) adder_1 (.a(A), .b(B), .out(adder_1_out), .cin(Cin), .cout(adder_1_cout));
  Multiplier #(.width(1)) multiplier_1 (
    .a(A), .b(B), .out(multiplier_1_out), .cin(subtractor_1_bout), .cout(multiplier_1_cout));
  not not_1 (not_1_out, A);
  and and_1 (and_1_out, A, B);
  or or_1 (or_1_out, A, B);
  nor nor_1 (nor_1_out, A, B);
  xor xor_1 (xor_1_out, A, B);
  xor xor_2 (xor_2_out, A, B);
  xnor xnor_1 (xnor_1_out, A, B);
  Subtractor #(.width(1)) subtractor_1 (
    .a(A), .b(B), .out(subtractor_1_out), .bin(adder_1_cout), .bout(subtractor_1_bout));
  Divider #(.width(1)) divider_1 (.a(A), .b(B), .out(divider_1_out), .upper(multiplier_1_cout), .rem(Cout));
  nand nand_1 (nand_1_out, A, B);
  Multiplexer #(.select(4)) multiplexer_1 (
    .in0(not_1_out), .in2(and_1_out), .in3(or_1_out), .in4(nand_1_out), .in5(nor_1_out), .in6(xor_1_out),
    .in7(xor_2_out), .in8(xnor_1_out), .in9(adder_1_out), .in10(subtractor_1_out), .in11(multiplier_1_out),
    .in14(divider_1_out), .out(Output), .sel(S));  // open: in1, in12, in13, in15, en

  // Notes on the sheet:
  //   1 bit alu using all gates and arthimatic circuit
endmodule

module _16_bit_ALU (
  input  in_1,
  input  [3:0] in_2,
  input  [15:0] in_3,
  input  [15:0] in_4,
  output [15:0] out_5,
  output out_6
);

  wire alu_consist_all_logic_1_cout, alu_consist_all_logic_2_cout, alu_consist_all_logic_3_cout,
       alu_consist_all_logic_4_cout, alu_consist_all_logic_5_cout, alu_consist_all_logic_6_cout,
       alu_consist_all_logic_7_cout, alu_consist_all_logic_8_cout, alu_consist_all_logic_9_cout,
       alu_consist_all_logic_10_cout, alu_consist_all_logic_11_cout, alu_consist_all_logic_12_cout,
       alu_consist_all_logic_13_cout, alu_consist_all_logic_14_cout, alu_consist_all_logic_15_cout;

  ALU_consist_All_Logic_Gate alu_consist_all_logic_1 (
    .A(in_3[0]), .Cin(in_1), .B(in_4[0]), .Output(out_5[0]), .S(in_2), .Cout(alu_consist_all_logic_1_cout));
  ALU_consist_All_Logic_Gate alu_consist_all_logic_2 (
    .A(in_3[2]), .Cin(alu_consist_all_logic_9_cout), .B(in_4[2]), .Output(out_5[2]), .S(in_2),
    .Cout(alu_consist_all_logic_2_cout));
  ALU_consist_All_Logic_Gate alu_consist_all_logic_3 (
    .A(in_3[4]), .Cin(alu_consist_all_logic_10_cout), .B(in_4[4]), .Output(out_5[4]), .S(in_2),
    .Cout(alu_consist_all_logic_3_cout));
  ALU_consist_All_Logic_Gate alu_consist_all_logic_4 (
    .A(in_3[6]), .Cin(alu_consist_all_logic_11_cout), .B(in_4[5]), .Output(out_5[6]), .S(in_2),
    .Cout(alu_consist_all_logic_4_cout));
  ALU_consist_All_Logic_Gate alu_consist_all_logic_5 (
    .A(in_3[8]), .Cin(alu_consist_all_logic_12_cout), .B(in_4[8]), .Output(out_5[8]), .S(in_2),
    .Cout(alu_consist_all_logic_5_cout));
  ALU_consist_All_Logic_Gate alu_consist_all_logic_6 (
    .A(in_3[10]), .Cin(alu_consist_all_logic_13_cout), .B(in_4[10]), .Output(out_5[10]), .S(in_2),
    .Cout(alu_consist_all_logic_6_cout));
  ALU_consist_All_Logic_Gate alu_consist_all_logic_7 (
    .A(in_3[12]), .Cin(alu_consist_all_logic_14_cout), .B(in_4[12]), .Output(out_5[12]), .S(in_2),
    .Cout(alu_consist_all_logic_7_cout));
  ALU_consist_All_Logic_Gate alu_consist_all_logic_8 (
    .A(in_3[14]), .Cin(alu_consist_all_logic_15_cout), .B(in_4[14]), .Output(out_5[14]), .S(in_2),
    .Cout(alu_consist_all_logic_8_cout));
  ALU_consist_All_Logic_Gate alu_consist_all_logic_9 (
    .A(in_3[1]), .Cin(alu_consist_all_logic_1_cout), .B(in_4[1]), .Output(out_5[1]), .S(in_2),
    .Cout(alu_consist_all_logic_9_cout));
  ALU_consist_All_Logic_Gate alu_consist_all_logic_10 (
    .A(in_3[3]), .Cin(alu_consist_all_logic_2_cout), .B(in_4[3]), .Output(out_5[3]), .S(in_2),
    .Cout(alu_consist_all_logic_10_cout));
  ALU_consist_All_Logic_Gate alu_consist_all_logic_11 (
    .A(in_3[5]), .Cin(alu_consist_all_logic_3_cout), .B(in_4[6]), .Output(out_5[5]), .S(in_2),
    .Cout(alu_consist_all_logic_11_cout));
  ALU_consist_All_Logic_Gate alu_consist_all_logic_12 (
    .A(in_3[7]), .Cin(alu_consist_all_logic_4_cout), .B(in_4[7]), .Output(out_5[7]), .S(in_2),
    .Cout(alu_consist_all_logic_12_cout));
  ALU_consist_All_Logic_Gate alu_consist_all_logic_13 (
    .A(in_3[9]), .Cin(alu_consist_all_logic_5_cout), .B(in_4[9]), .Output(out_5[9]), .S(in_2),
    .Cout(alu_consist_all_logic_13_cout));
  ALU_consist_All_Logic_Gate alu_consist_all_logic_14 (
    .A(in_3[11]), .Cin(alu_consist_all_logic_6_cout), .B(in_4[11]), .Output(out_5[11]), .S(in_2),
    .Cout(alu_consist_all_logic_14_cout));
  ALU_consist_All_Logic_Gate alu_consist_all_logic_15 (
    .A(in_3[13]), .Cin(alu_consist_all_logic_7_cout), .B(in_4[13]), .Output(out_5[13]), .S(in_2),
    .Cout(alu_consist_all_logic_15_cout));
  ALU_consist_All_Logic_Gate alu_consist_all_logic_16 (
    .A(in_3[15]), .Cin(alu_consist_all_logic_8_cout), .B(in_4[15]), .Output(out_5[15]), .S(in_2), .Cout(out_6));
endmodule

module DATA_PATH_ARCHITECTURE (
  input  [3:0] in_1,
  input  in_2,
  input  in_3,
  input  [3:0] in_4,
  input  in_5,
  input  in_6,
  input  in_7,
  input  in_8,
  input  [3:0] in_9,
  input  in_10,
  input  [3:0] in_11,
  input  [3:0] in_12,
  input  in_13,
  output [3:0] out_14,
  output [3:0] out_15,
  output [3:0] out_16,
  output [3:0] out_17,
  output [3:0] out_18,
  output [3:0] out_19
);

  wire clock_1_out, clock_2_out;
  wire [3:0] adder_1_out, multiplexer_1_out, multiplexer_2_out, subtractor_1_out;

  Demultiplexer #(.width(4)) demultiplexer_1 (.out0(out_14), .out1(in_4), .in(out_18), .sel(in_5));  // open: en
  Register #(.width(4)) Data_Register_1 (.D(out_18), .en(in_6), .Q(out_16), .clk(clock_1_out));  // open: clr
  Register #(.width(4), .trigger("falling")) Data_Register_2 (
    .D(out_18), .en(in_8), .Q(out_17), .clk(clock_1_out));  // open: clr
  Counter #(.width(4), .max('hf), .ongoal("load")) Program_Counter (
    .load(in_10), .D(in_11), .count(in_13), .Q(out_19), .clk(clock_1_out));  // open: carry, clr
  Clock clock_1 (.out(clock_1_out));
  Multiplexer #(.select(4), .width(4)) multiplexer_1 (
    .in0(out_17), .in1(out_19), .out(multiplexer_1_out), .sel(in_12));  // open: in2, in3, in4, in5, in6, in7, in8, in9, in10, in11, in12, in13, in14, in15, en
  Adder #(.width(4)) adder_1 (.a(out_16), .b(multiplexer_1_out), .out(adder_1_out));  // open: cin, cout
  Subtractor #(.width(4)) subtractor_1 (.a(out_16), .b(multiplexer_1_out), .out(subtractor_1_out));  // open: bin, bout
  Clock clock_2 (.out(clock_2_out));
  RAM #(.addrWidth(4), .dataWidth(4)) ram_1 (
    .addr(in_1), .data(out_15), .sel(in_2), .ld(clock_2_out), .clr(in_3));  // open: clk
  Multiplexer #(.select(4), .width(4)) multiplexer_2 (
    .in0(adder_1_out), .in1(subtractor_1_out), .in2(multiplexer_1_out), .out(multiplexer_2_out), .sel(in_9));  // open: in3, in4, in5, in6, in7, in8, in9, in10, in11, in12, in13, in14, in15, en
  Multiplexer #(.width(4)) multiplexer_3 (.in0(out_15), .in1(multiplexer_2_out), .out(out_18), .sel(in_7));  // open: en

  // Notes on the sheet:
  //   Data Path Architecture
endmodule
